# Fritzing sketch home_security_system (saved by Fritzing 0.9.0b)
breadboards: 1

parts:
  Part1 = Breakout Board for Electret Microphone
  R2 = Resistor [tolerance=±5% resistance=2.2k package=THT]
  Piezo1 = Piezo Speaker - PC Mount [part_number=COM-07950]
  BeagleBone2 = BeagleBone Black
  R3 = Resistor [tolerance=±5% resistance=56 package=THT]
  LED1 = LED - 5mm [color="Red (633nm)" package="5 mm [THT]"]

nets:
  N1: Part1.VCC, BeagleBone2.no_name_yet#36
  N2: Part1.GND, R2.Pin_0
  N3: Part1.AUD, BeagleBone2.no_name_yet#32
  N4: R2.Pin_1, Piezo1.VCC, BeagleBone2.no_name_yet#1, LED1.cathode
  N5: Piezo1.GND, BeagleBone2.no_name_yet#14
  N6: BeagleBone2.no_name_yet#41, R3.Pin_1
  N7: R3.Pin_0, LED1.anode

custom parts:
  Piezo Speaker - PC Mount: This is a small 12mm round speaker that operates around the audible 2kHz range. You can use these speakers to create simple music or user interfaces. Each speaker is PTH solderable and requires an operating voltage of 3.5-5V with a mean current of 35mA max. These speakers also have a typical sound output of 95 dBA and a coil resistance of 42 ±6.3 ohms.
  BeagleBone Black: BeagleBone Black rev. A5B
