# Fritzing sketch hookup_diagram_step_3 (saved by Fritzing 0.9.0b)
breadboards: 1

parts:
  BeagleBone1 = BeagleBone Black
  J1 = Piezo Speaker
  PIR1 = PIR sensor
  R1 = Resistor [tolerance=±5% resistance=10k package=THT]
  Part1 = Breakout Board for Electret Microphone
  R2 = Resistor [tolerance=±5% resistance=2.2k package=THT]

nets:
  N1: BeagleBone1.no_name_yet#1, J1.pin1, PIR1.SIG, R2.Pin_1
  N2: BeagleBone1.no_name_yet#7, PIR1.VDD
  N3: BeagleBone1.no_name_yet#12, PIR1.GND, R1.Pin_0
  N4: BeagleBone1.no_name_yet#14, J1.pin2
  N5: BeagleBone1.no_name_yet#32, Part1.AUD
  N6: BeagleBone1.no_name_yet#36, Part1.VCC
  N7: Part1.GND, R2.Pin_0

custom parts:
  BeagleBone Black: BeagleBone Black rev. A5B
