# Fritzing sketch hookup_diagram_step_2 (saved by Fritzing 0.8.7b)
breadboards: 1

parts:
  BeagleBone1 = BeagleBone Black
  J1 = Piezo Speaker
  PIR1 = PIR sensor
  R1 = Resistor [tolerance=±5% resistance=10k package=THT]

nets:
  N1: BeagleBone1.no_name_yet#1, J1.pin1, PIR1.SIG
  N2: BeagleBone1.no_name_yet#7, PIR1.VDD
  N3: BeagleBone1.no_name_yet#12, PIR1.GND, R1.Pin_0
  N4: BeagleBone1.no_name_yet#14, J1.pin2

custom parts:
  BeagleBone Black: BeagleBone Black rev. A5B
